// Logisim project Guia_0501.circ as structural Verilog: 1 circuit, main circuit main
module main (
  input  in_1,
  input  in_2,
  output out_3,
  output a___b__prime
);

  wire not_1_out, not_2_out;

  not not_1 (not_1_out, in_2);
  not not_2 (not_2_out, in_1);
  and and_1 (out_3, in_1, not_1_out);
  nor nor_1 (a___b__prime, in_2, not_2_out);

  // Notes on the sheet:
  //   Ricardo Soares Cerqueira$803833
  //   original (a & b')
endmodule
