// Logisim project Guia_07.circ as structural Verilog: 6 circuits, main circuit main
module main (
  input  a,
  input  b,
  input  select_1,
  input  select_2,
  input  select_3,
  output s1,
  output s2,
  output s3,
  output s4,
  output s5
);

  Q01___AND_NAND_MUX q01_and_nand_mux_1 (.a(b), .b(a), .select(select_1), .s1(s1));
  Q02___OR_NOR_MUX q02_or_nor_mux_1 (.in_1(b), .in_2(a), .in_3(select_1), .out_4(s2));
  Q03___OR_NOR_AND_NAND_MUX q03_or_nor_and_nand_mux_1 (
    .in_1(b), .in_2(a), .Select_1(select_1), .Select_2(select_2), .out_5(s3));
  Q04___OR_NOR_XOR_XNOR_MUX q04_or_nor_xor_xnor_mux_1 (
    .in_1(b), .in_2(a), .Select_1(select_1), .Select_2(select_2), .out_5(s4));
  Q05___EVERY_GATE_MUX q05_every_gate_mux_1 (
    .in_1(b), .in_2(a), .Select_1(select_1), .Select_2(select_2), .Select_3(select_3), .out_6(s5));

  // Notes on the sheet:
  //   Ricardo Soares Cerqueira$803833
  //   Q1
  //   Q2
endmodule

module Q01___AND_NAND_MUX (
  input  a,
  input  b,
  input  select,
  output s1
);

  wire and_1_out, nand_1_out;

  and and_1 (and_1_out, a, b);
  nand nand_1 (nand_1_out, a, b);
  Multiplexer #(.enable("false")) multiplexer_1 (.in0(and_1_out), .in1(nand_1_out), .out(s1), .sel(select));
endmodule

module Q02___OR_NOR_MUX (
  input  in_1,
  input  in_2,
  input  in_3,
  output out_4
);

  wire nor_1_out, or_1_out;

  or or_1 (or_1_out, in_1, in_2);
  nor nor_1 (nor_1_out, in_1, in_2);
  Multiplexer #(.enable("false")) multiplexer_1 (.in0(or_1_out), .in1(nor_1_out), .out(out_4), .sel(in_3));
endmodule

module Q03___OR_NOR_AND_NAND_MUX (
  input  in_1,
  input  in_2,
  input  Select_1,
  input  Select_2,
  output out_5
);

  wire and_1_out, multiplexer_1_out, multiplexer_2_out, nand_1_out, nor_1_out, or_1_out;

  or or_1 (or_1_out, in_1, in_2);
  nor nor_1 (nor_1_out, in_1, in_2);
  and and_1 (and_1_out, in_1, in_2);
  nand nand_1 (nand_1_out, in_1, in_2);
  Multiplexer #(.enable("false")) multiplexer_1 (
    .in0(or_1_out), .in1(nor_1_out), .out(multiplexer_1_out), .sel(Select_1));
  Multiplexer #(.enable("false")) multiplexer_2 (
    .in0(and_1_out), .in1(nand_1_out), .out(multiplexer_2_out), .sel(Select_1));
  Multiplexer #(.enable("false")) multiplexer_3 (
    .in0(multiplexer_1_out), .in1(multiplexer_2_out), .out(out_5), .sel(Select_2));
endmodule

module Q04___OR_NOR_XOR_XNOR_MUX (
  input  in_1,
  input  in_2,
  input  Select_1,
  input  Select_2,
  output out_5
);

  wire multiplexer_1_out, multiplexer_2_out, nor_1_out, or_1_out, xnor_1_out, xor_1_out;

  or or_1 (or_1_out, in_1, in_2);
  nor nor_1 (nor_1_out, in_1, in_2);
  xor xor_1 (xor_1_out, in_1, in_2);
  xnor xnor_1 (xnor_1_out, in_1, in_2);
  Multiplexer #(.enable("false")) multiplexer_1 (
    .in0(or_1_out), .in1(nor_1_out), .out(multiplexer_1_out), .sel(Select_1));
  Multiplexer #(.enable("false")) multiplexer_2 (
    .in0(xor_1_out), .in1(xnor_1_out), .out(multiplexer_2_out), .sel(Select_1));
  Multiplexer #(.enable("false")) multiplexer_3 (
    .in0(multiplexer_1_out), .in1(multiplexer_2_out), .out(out_5), .sel(Select_2));
endmodule

module Q05___EVERY_GATE_MUX (
  input  in_1,
  input  in_2,
  input  Select_1,
  input  Select_2,
  input  Select_3,
  output out_6
);

  wire and_1_out, multiplexer_1_out, multiplexer_2_out, multiplexer_3_out, multiplexer_4_out,
       multiplexer_5_out, multiplexer_6_out, nand_1_out, nor_1_out, not_1_out, or_1_out, xnor_1_out,
       xor_1_out;

  or or_1 (or_1_out, in_1, in_2);
  nor nor_1 (nor_1_out, in_1, in_2);
  and and_1 (and_1_out, in_1, in_2);
  nand nand_1 (nand_1_out, in_1, in_2);
  xor xor_1 (xor_1_out, in_1, in_2);
  xnor xnor_1 (xnor_1_out, in_1, in_2);
  not not_1 (not_1_out, in_2);
  Multiplexer #(.enable("false")) multiplexer_1 (
    .in0(or_1_out), .in1(nor_1_out), .out(multiplexer_1_out), .sel(Select_1));
  Multiplexer #(.enable("false")) multiplexer_2 (
    .in0(and_1_out), .in1(nand_1_out), .out(multiplexer_2_out), .sel(Select_1));
  Multiplexer #(.enable("false")) multiplexer_3 (
    .in0(xor_1_out), .in1(xnor_1_out), .out(multiplexer_3_out), .sel(Select_1));
  Multiplexer #(.enable("false")) multiplexer_4 (
    .in0(xnor_1_out), .in1(not_1_out), .out(multiplexer_4_out), .sel(Select_1));
  Multiplexer #(.enable("false")) multiplexer_5 (
    .in0(multiplexer_1_out), .in1(multiplexer_2_out), .out(multiplexer_5_out), .sel(Select_2));
  Multiplexer #(.enable("false")) multiplexer_6 (
    .in0(multiplexer_3_out), .in1(multiplexer_4_out), .out(multiplexer_6_out), .sel(Select_2));
  Multiplexer #(.enable("false")) multiplexer_7 (
    .in0(multiplexer_5_out), .in1(multiplexer_6_out), .out(out_6), .sel(Select_3));
endmodule
