// Logisim project Guia_0801.circ as structural Verilog: 2 circuits, main circuit main
module main (
  input  in_1,
  input  in_2,
  input  in_3,
  input  in_4,
  input  in_5,
  input  in_6,
  input  in_7,
  input  in_8,
  input  in_9,
  input  in_10,
  output out_11,
  output out_12,
  output out_13,
  output out_14,
  output out_15,
  output out_16
);

  wire halfadder_2_carry_out, halfadder_3_carry_out, halfadder_4_carry_out, halfadder_5_carry_out;

  HalfAdder halfadder_1 (.x(in_1), .y(in_6), .carry_in(halfadder_2_carry_out), .s(out_12), .carry_out(out_11));
  HalfAdder halfadder_2 (
    .x(in_2), .y(in_7), .carry_in(halfadder_3_carry_out), .s(out_13), .carry_out(halfadder_2_carry_out));
  HalfAdder halfadder_3 (
    .x(in_3), .y(in_8), .carry_in(halfadder_5_carry_out), .s(out_14), .carry_out(halfadder_3_carry_out));
  HalfAdder halfadder_4 (.x(in_5), .y(in_10), .carry_in(1'b0), .s(out_16), .carry_out(halfadder_4_carry_out));
  HalfAdder halfadder_5 (
    .x(in_9), .y(in_4), .carry_in(halfadder_4_carry_out), .s(out_15), .carry_out(halfadder_5_carry_out));

  // Notes on the sheet:
  //   803833 - Ricardo Soares Cerqueira
endmodule

module HalfAdder (
  input  x,
  input  y,
  input  carry_in,
  output s,
  output carry_out
);

  wire and_1_out, and_2_out, xor_1_out;

  xor xor_1 (xor_1_out, x, y);
  and and_1 (and_1_out, x, y);
  xor xor_2 (s, carry_in, xor_1_out);
  and and_2 (and_2_out, xor_1_out, carry_in);
  or or_1 (carry_out, and_2_out, and_1_out);
endmodule
