// Logisim project Guia_0802.circ as structural Verilog: 3 circuits, main circuit main
module main (
  input  in_1,
  input  in_2,
  input  in_3,
  input  in_4,
  input  in_5,
  input  in_6,
  input  in_7,
  input  in_8,
  input  in_9,
  input  in_10,
  output out_11,
  output out_12,
  output out_13,
  output out_14,
  output out_15
);

  wire full_subtractor_1_carry_out, full_subtractor_2_carry_out, full_subtractor_3_carry_out,
       full_subtractor_4_carry_out;

  full_subtractor full_subtractor_1 (
    .a(1'b0), .b(in_6), .carry_in(in_1), .carry_out(full_subtractor_1_carry_out), .diff(out_11));
  full_subtractor full_subtractor_2 (
    .a(full_subtractor_1_carry_out), .b(in_7), .carry_in(in_2), .carry_out(full_subtractor_2_carry_out),
    .diff(out_12));
  full_subtractor full_subtractor_3 (
    .a(full_subtractor_4_carry_out), .b(in_4), .carry_in(in_9), .carry_out(full_subtractor_3_carry_out),
    .diff(out_14));
  full_subtractor full_subtractor_4 (
    .a(full_subtractor_2_carry_out), .b(in_8), .carry_in(in_3), .carry_out(full_subtractor_4_carry_out),
    .diff(out_13));
  full_subtractor full_subtractor_5 (
    .a(full_subtractor_3_carry_out), .b(in_10), .carry_in(in_5), .diff(out_15));  // open: carry_out

  // Notes on the sheet:
  //   803833 - Ricardo Soares Cerqueira
endmodule

module half_subtractor (
  input  a,
  input  b,
  output out_3,
  output out_4
);

  wire not_1_out;

  xor xor_1 (out_3, a, b);
  and and_1 (out_4, b, not_1_out);
  not not_1 (not_1_out, a);
endmodule

module full_subtractor (
  input  a,
  input  b,
  input  carry_in,
  output carry_out,
  output diff
);

  wire half_subtractor_1_out_3, half_subtractor_1_out_4, half_subtractor_2_out_4;

  half_subtractor half_subtractor_1 (.a(a), .b(b), .out_3(half_subtractor_1_out_3), .out_4(half_subtractor_1_out_4));
  half_subtractor half_subtractor_2 (
    .a(carry_in), .b(half_subtractor_1_out_3), .out_3(diff), .out_4(half_subtractor_2_out_4));
  or or_1 (carry_out, half_subtractor_2_out_4, half_subtractor_1_out_4);
endmodule
