// Logisim project Guia_0803.circ as structural Verilog: 2 circuits, main circuit main
module main (
  input  in_1,
  input  in_2,
  input  in_3,
  input  in_4,
  input  in_5,
  input  in_6,
  input  in_7,
  input  in_8,
  input  in_9,
  input  in_10,
  output out_11
);

  wire igualdade_xnor_1_out_3, igualdade_xnor_2_out_3, igualdade_xnor_3_out_3, igualdade_xnor_4_out_3,
       igualdade_xnor_5_out_3;

  Igualdade__XNOR igualdade_xnor_1 (.in_1(in_6), .in_2(in_1), .out_3(igualdade_xnor_1_out_3));
  Igualdade__XNOR igualdade_xnor_2 (.in_1(in_7), .in_2(in_2), .out_3(igualdade_xnor_2_out_3));
  Igualdade__XNOR igualdade_xnor_3 (.in_1(in_8), .in_2(in_3), .out_3(igualdade_xnor_3_out_3));
  or or_1 (out_11, igualdade_xnor_1_out_3, igualdade_xnor_2_out_3, igualdade_xnor_3_out_3, igualdade_xnor_4_out_3, igualdade_xnor_5_out_3);
  Igualdade__XNOR igualdade_xnor_4 (.in_1(in_4), .in_2(in_9), .out_3(igualdade_xnor_4_out_3));
  Igualdade__XNOR igualdade_xnor_5 (.in_1(in_10), .in_2(in_5), .out_3(igualdade_xnor_5_out_3));

  // Notes on the sheet:
  //   803833 - Ricardo Soares Cerqueira
endmodule

module Igualdade__XNOR (
  input  in_1,
  input  in_2,
  output out_3
);

  xnor xnor_1 (out_3, in_1, in_2);
endmodule
