// Logisim project Guia_0804.circ as structural Verilog: 2 circuits, main circuit main
module main (
  input  in_1,
  input  in_2,
  input  in_3,
  input  in_4,
  input  in_5,
  input  in_6,
  input  in_7,
  input  in_8,
  input  in_9,
  input  in_10,
  output out_11
);

  wire desigualdade_xor_1_out_3, desigualdade_xor_2_out_3, desigualdade_xor_3_out_3,
       desigualdade_xor_4_out_3, desigualdade_xor_5_out_3;

  Desigualdade__XOR desigualdade_xor_1 (.a(in_6), .b(in_1), .out_3(desigualdade_xor_1_out_3));
  Desigualdade__XOR desigualdade_xor_2 (.a(in_7), .b(in_2), .out_3(desigualdade_xor_2_out_3));
  Desigualdade__XOR desigualdade_xor_3 (.a(in_8), .b(in_3), .out_3(desigualdade_xor_3_out_3));
  or or_1 (out_11, desigualdade_xor_1_out_3, desigualdade_xor_2_out_3, desigualdade_xor_3_out_3, desigualdade_xor_4_out_3, desigualdade_xor_5_out_3);
  Desigualdade__XOR desigualdade_xor_4 (.a(in_4), .b(in_9), .out_3(desigualdade_xor_4_out_3));
  Desigualdade__XOR desigualdade_xor_5 (.a(in_10), .b(in_5), .out_3(desigualdade_xor_5_out_3));

  // Notes on the sheet:
  //   803833 - Ricardo Soares Cerqueira
endmodule

module Desigualdade__XOR (
  input  a,
  input  b,
  output out_3
);

  xor xor_1 (out_3, a, b);
endmodule
