// Logisim project Guia_0805.circ as structural Verilog: 3 circuits, main circuit main
module main (
  input  in_1,
  input  in_2,
  input  in_3,
  input  in_4,
  input  in_5,
  output out_6,
  output out_7,
  output out_8,
  output out_9,
  output out_10
);

  wire complemento_de_1_1_out_6, complemento_de_1_1_out_7, complemento_de_1_1_out_8,
       complemento_de_1_1_out_9, complemento_de_1_1_out_10, full_adder_2_carry_out, full_adder_3_carry_out,
       full_adder_4_carry_out, full_adder_5_carry_out;

  full_Adder full_adder_1 (
    .x(complemento_de_1_1_out_6), .y(1'b0), .carry_in(full_adder_2_carry_out), .s(out_6));  // open: carry_out
  Complemento_de_1 complemento_de_1_1 (
    .in_1(in_1), .in_2(in_2), .in_3(in_3), .in_4(in_4), .in_5(in_5), .out_6(complemento_de_1_1_out_6),
    .out_7(complemento_de_1_1_out_7), .out_8(complemento_de_1_1_out_8), .out_9(complemento_de_1_1_out_9),
    .out_10(complemento_de_1_1_out_10));
  full_Adder full_adder_2 (
    .x(complemento_de_1_1_out_7), .y(1'b0), .carry_in(full_adder_3_carry_out), .s(out_7),
    .carry_out(full_adder_2_carry_out));
  full_Adder full_adder_3 (
    .x(complemento_de_1_1_out_8), .y(1'b0), .carry_in(full_adder_4_carry_out), .s(out_8),
    .carry_out(full_adder_3_carry_out));
  full_Adder full_adder_4 (
    .x(complemento_de_1_1_out_9), .y(1'b0), .carry_in(full_adder_5_carry_out), .s(out_9),
    .carry_out(full_adder_4_carry_out));
  full_Adder full_adder_5 (
    .x(complemento_de_1_1_out_10), .y(1'b1), .carry_in(1'b0), .s(out_10), .carry_out(full_adder_5_carry_out));

  // Notes on the sheet:
  //   803833 - Ricardo Soares Cerqueira
endmodule

module Complemento_de_1 (
  input  in_1,
  input  in_2,
  input  in_3,
  input  in_4,
  input  in_5,
  output out_6,
  output out_7,
  output out_8,
  output out_9,
  output out_10
);

  not not_1 (out_6, in_1);
  not not_2 (out_7, in_2);
  not not_3 (out_8, in_3);
  not not_4 (out_9, in_4);
  not not_5 (out_10, in_5);
endmodule

module full_Adder (
  input  x,
  input  y,
  input  carry_in,
  output s,
  output carry_out
);

  wire and_1_out, and_2_out, xor_1_out;

  xor xor_1 (xor_1_out, x, y);
  and and_1 (and_1_out, x, y);
  xor xor_2 (s, carry_in, xor_1_out);
  and and_2 (and_2_out, xor_1_out, carry_in);
  or or_1 (carry_out, and_2_out, and_1_out);
endmodule
