// Logisim project Somador completo.circ as structural Verilog: 5 circuits, main circuit main
module main (
  input  a3,
  input  a2,
  input  a1,
  input  a0,
  input  b3,
  input  b2,
  input  b1,
  input  b0,
  input  CarryIn,
  output s3,
  output s2,
  output s1,
  output s0,
  output CarryOut
);

  wire decoder_1_a, decoder_1_b, decoder_1_c, decoder_1_d, decoder_1_e, decoder_1_f, decoder_1_g,
       decoder_2_a, decoder_2_b, decoder_2_c, decoder_2_d, decoder_2_e, decoder_2_f, decoder_2_g,
       decoder_3_a, decoder_3_b, decoder_3_c, decoder_3_d, decoder_3_e, decoder_3_f, decoder_3_g;

  Decoder decoder_1 (
    .e0(a0), .e1(a1), .e2(a2), .e3(a3), .b(decoder_1_b), .a(decoder_1_a), .f(decoder_1_f), .g(decoder_1_g),
    .e(decoder_1_e), .d(decoder_1_d), .c(decoder_1_c));
  _7_Segment_Display u_7_segment_display_1 (
    .g(decoder_1_g), .f(decoder_1_f), .a(decoder_1_a), .b(decoder_1_b), .e(decoder_1_e), .d(decoder_1_d),
    .c(decoder_1_c));  // open: dp
  _4Bit_Adder u_4bit_adder_1 (
    .CarryOut(CarryOut), .a3(a3), .a2(a2), .a1(a1), .a0(a0), .b3(b3), .b2(b2), .b1(b1), .b0(b0), .s3(s3),
    .s2(s2), .s1(s1), .s0(s0), .CarryIn(CarryIn));
  Decoder decoder_2 (
    .e0(b0), .e1(b1), .e2(b2), .e3(b3), .b(decoder_2_b), .a(decoder_2_a), .f(decoder_2_f), .g(decoder_2_g),
    .e(decoder_2_e), .d(decoder_2_d), .c(decoder_2_c));
  _7_Segment_Display u_7_segment_display_2 (
    .g(decoder_2_g), .f(decoder_2_f), .a(decoder_2_a), .b(decoder_2_b), .e(decoder_2_e), .d(decoder_2_d),
    .c(decoder_2_c));  // open: dp
  Decoder decoder_3 (
    .e0(s0), .e1(s1), .e2(s2), .e3(s3), .b(decoder_3_b), .a(decoder_3_a), .f(decoder_3_f), .g(decoder_3_g),
    .e(decoder_3_e), .d(decoder_3_d), .c(decoder_3_c));
  _7_Segment_Display u_7_segment_display_3 (
    .g(decoder_3_g), .f(decoder_3_f), .a(decoder_3_a), .b(decoder_3_b), .e(decoder_3_e), .d(decoder_3_d),
    .c(decoder_3_c));  // open: dp

  // Notes on the sheet:
  //   +
  //   +
  //   =
  //   =
  //   Ricardo Soares Cerqueira$803833
endmodule

module Half_Adder (
  input  a,
  input  b,
  output Soma,
  output CarryOut
);

  and and_1 (CarryOut, b, a);
  xor xor_1 (Soma, a, b);
endmodule

module Full_Adder (
  input  CarryIn,
  input  b,
  input  a,
  output Soma,
  output CarryOut
);

  wire half_adder_1_carryout, half_adder_1_soma, half_adder_2_carryout;

  Half_Adder half_adder_1 (.a(b), .b(a), .CarryOut(half_adder_1_carryout), .Soma(half_adder_1_soma));
  or or_1 (CarryOut, half_adder_1_carryout, half_adder_2_carryout);
  Half_Adder half_adder_2 (.a(CarryIn), .b(half_adder_1_soma), .CarryOut(half_adder_2_carryout), .Soma(Soma));
endmodule

module _4Bit_Adder (
  input  a3,
  input  a2,
  input  a1,
  input  a0,
  input  b3,
  input  b2,
  input  b1,
  input  b0,
  input  CarryIn,
  output CarryOut,
  output s3,
  output s2,
  output s1,
  output s0
);

  wire full_adder_2_carryout, full_adder_3_carryout, full_adder_4_carryout;

  Full_Adder full_adder_1 (.b(b3), .a(a3), .CarryIn(full_adder_3_carryout), .CarryOut(CarryOut), .Soma(s3));
  Full_Adder full_adder_2 (
    .b(b1), .a(a1), .CarryIn(full_adder_4_carryout), .CarryOut(full_adder_2_carryout), .Soma(s1));
  Full_Adder full_adder_3 (
    .b(b2), .a(a2), .CarryIn(full_adder_2_carryout), .CarryOut(full_adder_3_carryout), .Soma(s2));
  Full_Adder full_adder_4 (.b(b0), .a(a0), .CarryIn(CarryIn), .CarryOut(full_adder_4_carryout), .Soma(s0));
endmodule

module Decoder (
  input  e0,
  input  e1,
  input  e2,
  input  e3,
  output b,
  output a,
  output f,
  output g,
  output e,
  output d,
  output c
);

  wire and_1_out, and_2_out, and_3_out, and_4_out, and_5_out, and_6_out, and_7_out, and_8_out, and_9_out,
       and_10_out, and_11_out, and_12_out, and_13_out, and_14_out, and_15_out, and_16_out, and_17_out,
       and_18_out, and_19_out, and_20_out, and_21_out, and_22_out, and_23_out, and_24_out, and_25_out,
       and_26_out, and_27_out, and_28_out, and_29_out, and_30_out, and_31_out, and_32_out, and_33_out,
       and_34_out, and_35_out, not_1_out, not_2_out, not_3_out, not_4_out, not_5_out, not_6_out, not_7_out,
       not_8_out, not_9_out, not_10_out, not_11_out, not_12_out, not_13_out, not_14_out, not_15_out,
       not_16_out, not_17_out, not_18_out, not_19_out, not_20_out, not_21_out, not_22_out, not_23_out,
       not_24_out, not_25_out, not_26_out, not_27_out, not_28_out, not_29_out, not_30_out, not_31_out,
       not_32_out, not_33_out, not_34_out, not_35_out, not_36_out, not_37_out, not_38_out, not_39_out,
       not_40_out, not_41_out, not_42_out, not_43_out;

  not not_1 (not_1_out, e3);
  and and_1 (and_1_out, not_1_out, not_2_out);
  not not_2 (not_2_out, e2);
  not not_3 (not_3_out, e3);
  and and_2 (and_2_out, not_3_out, not_4_out, not_5_out);
  not not_4 (not_4_out, e1);
  not not_5 (not_5_out, e0);
  not not_6 (not_6_out, e2);
  and and_3 (and_3_out, not_6_out, not_7_out);
  not not_7 (not_7_out, e0);
  not not_8 (not_8_out, e3);
  and and_4 (and_4_out, not_8_out, e1, e0);
  not not_9 (not_9_out, e1);
  and and_5 (and_5_out, e3, not_9_out, e0);
  not not_10 (not_10_out, e2);
  and and_6 (and_6_out, not_10_out, not_11_out);
  not not_11 (not_11_out, e0);
  not not_12 (not_12_out, e3);
  and and_7 (and_7_out, not_12_out, e1);
  not not_13 (not_13_out, e3);
  and and_8 (and_8_out, not_13_out, e2, e0);
  and and_9 (and_9_out, e2, e1);
  and and_10 (and_10_out, e3, not_14_out, not_15_out);
  not not_14 (not_14_out, e2);
  not not_15 (not_15_out, e1);
  and and_11 (and_11_out, e3, not_16_out);
  not not_16 (not_16_out, e0);
  not not_17 (not_17_out, e1);
  and and_12 (and_12_out, not_17_out, not_18_out);
  not not_18 (not_18_out, e0);
  not not_19 (not_19_out, e3);
  and and_13 (and_13_out, not_19_out, e2, not_20_out);
  not not_20 (not_20_out, e1);
  and and_14 (and_14_out, e2, not_21_out);
  not not_21 (not_21_out, e0);
  and and_15 (and_15_out, e3, not_22_out);
  not not_22 (not_22_out, e2);
  and and_16 (and_16_out, e3, e1);
  not not_23 (not_23_out, e2);
  and and_17 (and_17_out, not_23_out, e1);
  and and_18 (and_18_out, e1, not_24_out);
  not not_24 (not_24_out, e0);
  not not_25 (not_25_out, e3);
  and and_19 (and_19_out, not_25_out, e2, not_26_out);
  not not_26 (not_26_out, e1);
  and and_20 (and_20_out, e3, not_27_out);
  not not_27 (not_27_out, e2);
  and and_21 (and_21_out, e3, e0);
  not not_28 (not_28_out, e2);
  and and_22 (and_22_out, not_28_out, not_29_out);
  not not_29 (not_29_out, e0);
  and and_23 (and_23_out, e1, not_30_out);
  not not_30 (not_30_out, e0);
  and and_24 (and_24_out, e3, e1);
  and and_25 (and_25_out, e3, e2);
  not not_31 (not_31_out, e3);
  not not_32 (not_32_out, e2);
  and and_26 (and_26_out, not_31_out, not_32_out, not_33_out);
  not not_33 (not_33_out, e0);
  not not_34 (not_34_out, e2);
  and and_27 (and_27_out, not_34_out, e1, e0);
  not not_35 (not_35_out, e1);
  and and_28 (and_28_out, e2, not_35_out, e0);
  and and_29 (and_29_out, e2, e1, not_36_out);
  not not_36 (not_36_out, e0);
  and and_30 (and_30_out, e3, not_37_out);
  not not_37 (not_37_out, e1);
  not not_38 (not_38_out, e3);
  and and_31 (and_31_out, not_38_out, not_39_out);
  not not_39 (not_39_out, e1);
  not not_40 (not_40_out, e3);
  and and_32 (and_32_out, not_40_out, e0);
  not not_41 (not_41_out, e1);
  and and_33 (and_33_out, not_41_out, e0);
  not not_42 (not_42_out, e3);
  and and_34 (and_34_out, not_42_out, e2);
  and and_35 (and_35_out, e3, not_43_out);
  not not_43 (not_43_out, e2);
  or or_1 (b, and_1_out, and_2_out, and_3_out, and_4_out, and_5_out);
  or or_2 (f, and_12_out, and_13_out, and_14_out, and_15_out, and_16_out);
  or or_3 (g, and_17_out, and_18_out, and_19_out, and_20_out, and_21_out);
  or or_4 (e, and_22_out, and_23_out, and_24_out, and_25_out);
  or or_5 (d, and_26_out, and_27_out, and_28_out, and_29_out, and_30_out);
  or or_6 (c, and_31_out, and_32_out, and_33_out, and_34_out, and_35_out);
  or or_7 (a, and_6_out, and_7_out, and_8_out, and_9_out, and_10_out, and_11_out);
endmodule
