// Logisim project ULA.circ as structural Verilog: 6 circuits, main circuit main
module main (
  input  [3:0] A,
  input  [3:0] B,
  input  B_Invert,
  input  OP0,
  input  OP1,
  output [3:0] S,
  output CarryOut
);

  wire ula_1_carry_out, ula_2_carry_out, ula_3_carry_out;

  ULA ula_1 (
    .A(A[0]), .B(B[0]), .B_Invert(B_Invert), .CarryIn(B_Invert), .OP0(OP0), .OP1(OP1),
    .Carry_Out(ula_1_carry_out), .S(S[0]));
  ULA ula_2 (
    .A(A[1]), .B(B[1]), .B_Invert(B_Invert), .CarryIn(ula_1_carry_out), .OP0(OP0), .OP1(OP1),
    .Carry_Out(ula_2_carry_out), .S(S[1]));
  ULA ula_3 (
    .A(A[2]), .B(B[2]), .B_Invert(B_Invert), .CarryIn(ula_2_carry_out), .OP0(OP0), .OP1(OP1),
    .Carry_Out(ula_3_carry_out), .S(S[2]));
  ULA ula_4 (
    .A(A[3]), .B(B[3]), .B_Invert(B_Invert), .CarryIn(ula_3_carry_out), .OP0(OP0), .OP1(OP1),
    .Carry_Out(CarryOut), .S(S[3]));
endmodule

module ULA (
  input  B_Invert,
  input  CarryIn,
  input  OP0,
  input  OP1,
  input  A,
  input  B,
  output S,
  output Carry_Out
);

  wire and_1_out, full_adder_1_soma, mux_1bit_1_s, not_1_out, not_2_out, or_1_out;

  not not_1 (not_1_out, B);
  not not_2 (not_2_out, A);
  MUX_1BIT mux_1bit_1 (.A(B), .B(not_1_out), .Select(B_Invert), .S(mux_1bit_1_s));
  and and_1 (and_1_out, A, mux_1bit_1_s);
  or or_1 (or_1_out, A, mux_1bit_1_s);
  FULL_ADDER full_adder_1 (.b(A), .a(mux_1bit_1_s), .CarryIn(CarryIn), .CarryOut(Carry_Out), .Soma(full_adder_1_soma));
  MUX_4BIT mux_4bit_1 (
    .e1(and_1_out), .e2(or_1_out), .e3(not_2_out), .e4(full_adder_1_soma), .Select_0(OP0), .Select_1(OP1),
    .S(S));
endmodule

module MUX_1BIT (
  input  Select,
  input  A,
  input  B,
  output S
);

  wire and_1_out, and_2_out, not_1_out;

  not not_1 (not_1_out, Select);
  and and_1 (and_1_out, not_1_out, A);
  or or_1 (S, and_1_out, and_2_out);
  and and_2 (and_2_out, Select, B);
endmodule

module MUX_4BIT (
  input  Select_0,
  input  Select_1,
  input  e1,
  input  e2,
  input  e3,
  input  e4,
  output S
);

  wire and_1_out, and_2_out, and_3_out, and_4_out, not_1_out, not_2_out;

  not not_1 (not_1_out, Select_1);
  not not_2 (not_2_out, Select_0);
  and and_1 (and_1_out, not_1_out, not_2_out, e1);
  and and_2 (and_2_out, Select_1, not_2_out, e2);
  and and_3 (and_3_out, not_1_out, Select_0, e3);
  and and_4 (and_4_out, Select_1, Select_0, e4);
  or or_1 (S, and_1_out, and_2_out, and_3_out, and_4_out);
endmodule

module FULL_ADDER (
  input  CarryIn,
  input  b,
  input  a,
  output Soma,
  output CarryOut
);

  wire half_adder_1_carryout, half_adder_1_soma, half_adder_2_carryout;

  HALF_ADDER half_adder_1 (.a(b), .b(a), .CarryOut(half_adder_1_carryout), .Soma(half_adder_1_soma));
  or or_1 (CarryOut, half_adder_1_carryout, half_adder_2_carryout);
  HALF_ADDER half_adder_2 (.a(CarryIn), .b(half_adder_1_soma), .CarryOut(half_adder_2_carryout), .Soma(Soma));
endmodule

module HALF_ADDER (
  input  a,
  input  b,
  output Soma,
  output CarryOut
);

  and and_1 (CarryOut, b, a);
  xor xor_1 (Soma, a, b);
endmodule
